# Fritzing sketch Schaltplan_Luefter (saved by Fritzing 0.9.4)

parts:
  Serial = FTDI Basic Programmer
  Boot-Switch = Momentary Switch [package=ksa_sealed_tac_switch]
  Reset-Switch = Momentary Switch [package=ksa_sealed_tac_switch]
  R1 = Resistor [tolerance=±5% resistance=10k package="2512 [SMD]"]
  C1 = Capacitor Polarized [package=cpol-radial-10uf-25v]
  Controller = ESP8266 WiFi Module [part_number=ESP8266]
  R4 = Resistor [tolerance=±5% resistance=10k package=THT]
  R5 = Resistor [tolerance=±5% resistance=10k package=THT]
  R4_2 = Resistor [tolerance=±5% resistance=10k package=THT]
  Fan_connector = Fan - Ventilador [package=THT]
  R6 = Trimmer Potentiometer [maximum_resistance=10kΩ package=THT]
  C2 = Ceramic Capacitor [capacitance=100nF package="100 mil [THT, multilayer]"]
  J1 = Power Jack [package=power_jack_pth]
  U1 = LM2596 step down module
  Poti = POT [package=pot_alpha_rv16af-20]

nets:
  N1: Serial.RXI, Controller.TXD
  N2: Serial.TXO, Controller.RXD
  N3: Serial.POWER, R1.Pin_1, C1.+, Controller.VCC, R4.Pin_0, R4_2.Pin_1, R6.leg1, C2.0, U1.OUT+
  GND: Serial.GND, Boot-Switch.4, Reset-Switch.1, C1.-, Controller.GND, R5.Pin_1, Fan_connector.GND, R6.leg2, C2.1, J1.GND, U1.IN-, U1.OUT-, Poti.E
  N4: Boot-Switch.2, R1.Pin_0, Controller.CH_PD
  N5: Reset-Switch.3, Controller.GPIO_0, R4_2.Pin_0
  N6: Controller.GPIO_15, R5.Pin_0
  N7: Controller.GPIO_4, Fan_connector.PWM
  N8: Controller.GPIO_5, Fan_connector.Tacho
  N9: Controller.ADC_0, Poti.S
  N10: Controller.REST, R4.Pin_1
  12V: Fan_connector.5V, J1.PWR, U1.IN+
  N11: R6.wiper, Poti.A

custom parts:
  Fan - Ventilador: Ventilador de 2 pines, se encuentra comunmente en computadoras de escritorio
  LM2596 step down module: LM2596 DC-DC step down power supply module 3 A.
